# Fritzing sketch hardware (saved by Fritzing 0.9.4)
breadboards: 2

parts:
  U6 = Teensy 3.6 (Basic)
  U1 = 74HC595 [part_number="Sparkfun COM-13699" package="DIP16 [THT]"]
  U2 = Adafruit Si5351A Clock Generator [part_number="Adafruit #2045"]
  U5 = IC, DIP package, 24 pins [chip_label="YAMAHA YM2612"]
  U3 = Adafruit 4-channel I2C-safe Bi-directional Logic Level Converter [part_number="Adafruit #757"]
  U4 = TL072 [part_number=TL072 package=dip08]
  R1 = Resistor [tolerance=±5% resistance=2.2k package=THT]
  C1 = Electrolytic Capacitor [capacitance=10µF package="100 mil [THT, electrolytic]"]
  R2 = Resistor [tolerance=±5% resistance=4.7k package=THT]
  C2 = Electrolytic Capacitor [capacitance=1µF package="100 mil [THT, electrolytic]"]
  C3 = Electrolytic Capacitor [capacitance=1µF package="100 mil [THT, electrolytic]"]
  R3 = Resistor [tolerance=±5% resistance=330 package=THT]
  R4 = Resistor [tolerance=±5% resistance=2.2k package=THT]
  R5 = Resistor [tolerance=±5% resistance=220 package=THT]
  R6 = Resistor [tolerance=±5% resistance=220 package=THT]
  R7 = Resistor [tolerance=±5% resistance=4.7k package=THT]
  R8 = Resistor [tolerance=±5% resistance=470 package=THT]
  R9 = Resistor [tolerance=±5% resistance=680 package=THT]
  C5 = Electrolytic Capacitor [capacitance=100µF package="100 mil [THT, electrolytic]"]
  C6 = Ceramic Capacitor [capacitance=47pF package="100 mil [THT, multilayer]"]
  R11 = Resistor [tolerance=±5% resistance=100k package=THT]
  C7 = Ceramic Capacitor [capacitance=47pF package="100 mil [THT, multilayer]"]
  R12 = Resistor [tolerance=±5% resistance=300 package=THT]
  R13 = Resistor [tolerance=±5% resistance=300 package=THT]
  R14 = Resistor [tolerance=±5% resistance=300 package=THT]
  C8 = Electrolytic Capacitor [capacitance=220µF package="100 mil [THT, electrolytic]"]
  C9 = Electrolytic Capacitor [capacitance=220µF package="100 mil [THT, electrolytic]"]
  U7 = 2.5mm Audio Jack [package=stereojack2.5mm_specia_pogopins]
  R10 = Resistor [tolerance=±5% resistance=100k package=THT]
  C4 = Electrolytic Capacitor [capacitance=10µF package="100 mil [THT, electrolytic]"]

nets (from the breadboard view):
  GND: U6.GND, U1.GND, U1.OE, U2.GND, U5.pin1, U5.pin12, U5.pin14, U5.pin19, U3.GND, U4.VCC-, R1.Pin_0, R3.Pin_1, R4.Pin_1, R9.Pin_1, C5.-, R12.Pin_0, R13.Pin_0, R14.Pin_0, C8.-, C9.-, U7.SLEEVE
  N1: U6.A4/D18, U2.SDA
  N2: U6.A5/D19, U2.SCL
  N3: U6.A7/D21, U6.A11
  N4: U6.A8/D22, U6.A10
  N5: U6.A9/D23, U6.AREF
  3V3: U6.3V3, U6.3V3_1, U1.MR, U1.VCC, U2.VIN, U3.LV, C9.+
  N6: U6.AGND, U6.VUSB
  N7: U6.Vin, U5.pin16, U5.pin23, U3.HV, U4.VCC+, R8.Pin_0, C8.+
  N8: U6.D25, U3.A4
  N9: U6.D26, U3.A3
  N10: U6.D27, U6.3V, U6.Vb, U3.A2
  N11: U6.D28, U3.A1
  N12: U6.D30, U1.SH_CP, R14.Pin_1
  N13: U6.D31, U1.ST_CP, R13.Pin_1
  N14: U6.D32, U1.DS, R12.Pin_1
  N15: U6.D38, U6.R
  N16: U6.A21/DAC0, C2.-, C3.-, R3.Pin_0
  N17: U1.Q1, U5.pin3
  N18: U1.Q2, U5.pin4
  N19: U1.Q3, U5.pin5
  N20: U1.Q4, U5.pin6
  N21: U1.Q5, U5.pin7
  N22: U1.Q6, U5.pin8
  N23: U1.Q7, U5.pin9
  N24: U1.Q0, U5.pin2
  N25: U2.CLK0, U5.pin24
  N26: U5.pin11, U3.B1
  N27: U5.pin15, U3.B2
  N28: U5.pin17, U3.B3
  N29: U5.pin18, U3.B4
  N30: U5.pin20, R4.Pin_0, C4.+
  N31: U5.pin21, R1.Pin_1, C1.+
  N32: U4.1_OUT, R5.Pin_1, C6.1, U7.LEFT, R10.Pin_1
  N33: U4.1_IN-, R2.Pin_1, C6.0, R10.Pin_0
  N34: U4.1_IN+, U4.2_IN+, R8.Pin_1, R9.Pin_0, C5.+
  N35: U4.2_IN-, R6.Pin_1, R7.Pin_1, R11.Pin_0, C7.0
  N36: U4.2_OUT, R11.Pin_1, C7.1, U7.RIGHT
  N37: C1.-, R2.Pin_0
  N38: C2.+, R5.Pin_0
  N39: C3.+, R6.Pin_0
  N40: R7.Pin_0, C4.-

custom parts:
  Teensy 3.6 (Basic): The Teensy is a complete USB-based microcontoller development system, in a very small footprint, capable of implementing many types of projects. All programming is done via the USB port. No special programmer is needed, only a standard micro-USB cable and a PC or Macintosh with a USB port.
  Adafruit Si5351A Clock Generator: Never hunt around for another crystal again, with the Si5351A clock generator breakout from Adafruit! This chip has a precision 25MHz crystal reference and internal PLL and dividers so it can generate just about any frequency, from <8KHz up to 150+ MHz. The Si5351A clock generator is an I2C controller clock generator. It uses the onboard precision clock to drive multiple PLL's and clock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
  Adafruit 4-channel I2C-safe Bi-directional Logic Level Converter: Because the Arduino (and Basic Stamp) are 5V devices, and most modern sensors, displays, flash cards and modes are 3.3V-only, many makers find that they need to perform level shifting/conversion to protect the 3.3V device from 5V. We do have some other handy level shifters in the shop, from the DIP 74LVC245 to the fancy bi-directional TXB0108. However, neither of these are happy to work with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
  TL072: TL072 dual opamp
